# Fritzing sketch FlowerPowerCircuitBoard-v1 (saved by Fritzing 0.9.2b)
breadboards: 1

parts:
  REG1 = LD33 Low-Dropout Voltage Regulator
  PART1 = SparkFun Soil Moisture Sensor [part_number=SEN-13322]
  U1 = ESP8266 WiFi Module [part_number=ESP8266-07]
  C1 = Electrolytic Capacitor [capacitance=0.1mF voltage=16V package="100 mil [THT, electrolytic]"]
  C2 = Electrolytic Capacitor [capacitance=1mF package="100 mil [THT, electrolytic]"]
  BAT1 = Battery Holders [package=lipo-1100mAh]
  PART2 = SparkFun Soil Moisture Sensor [part_number=SEN-13322]
  JP1 = Header 3 [package=molex-1x3_lock]
  U2 = 74HC4051 [package=so16]
  C3 = Electrolytic Capacitor [capacitance=0.1mF voltage=16V package="100 mil [THT, electrolytic]"]
  PART3 = SparkFun Soil Moisture Sensor [part_number=SEN-13322]
  R1 = Resistor [tolerance=±5% resistance=240 part_number="R1 240Ω" package="1206 [SMD]"]
  R2 = Resistor [tolerance=±5% resistance=220 part_number="R2 240Ω" package="1206 [SMD]"]
  S1 = Toggle Switch [package=THT]

nets:
  GND: REG1.GND, PART1.GND, U1.GND, C1.-, C2.-, BAT1.-, PART2.GND, JP1.3, U2.IO5, U2.INH, U2.VEE, U2.VSS, C3.-, PART3.GND, PART3.SIG, R2.Pin_1
  VCC: REG1.Vout, PART1.VCC, U1.VCC, C2.+, PART2.VCC, PART3.VCC
  N1: REG1.Vin, C1.+, S1.COM
  N2: PART1.SIG, U2.IO4, U2.IO6
  N3: U1.RXD, JP1.2
  N4: U1.TXD, JP1.1
  N5: U1.ADC_0, R1.Pin_1, R2.Pin_0
  N6: U1.GPIO_16, U1.REST
  N7: U1.GPIO_14, U1.GPIO_12, U1.GPIO_13, U2.C, U2.B, U2.A, U2.IO3
  N8: BAT1.+, S1.L2
  N9: PART2.SIG, U2.IO7
  N10: U2.IO, R1.Pin_0
  N11: U2.IO2, U2.VDD, C3.+

notes:
  RX
  TX

custom parts:
  SparkFun Soil Moisture Sensor: The SparkFun Soil Moisture Sensor is a simple breakout for measuring the moisture in soil and similar materials.
